// Logisim project BCD_adder.circ as structural Verilog: 1 circuit, main circuit main
module main (
  input  Cin,
  input  [3:0] A,
  input  [3:0] B,
  output [3:0] Sum,
  output Final_carry
);

  wire adder_1_cout, adder_2_cout, and_1_out, and_2_out;
  wire [2:2] or_1_out;
  wire [3:0] adder_1_out;

  Adder #(.width(4)) adder_1 (.a(A), .b(B), .out(adder_1_out), .cin(Cin), .cout(adder_1_cout));
  and and_1 (and_1_out, adder_1_out[3], adder_1_out[2]);
  or or_1 (or_1_out[2], adder_1_cout, and_1_out, and_2_out);
  and and_2 (and_2_out, adder_1_out[3], adder_1_out[1]);
  Adder #(.width(4)) adder_2 (
    .a(adder_1_out), .b({1'b0, {2{or_1_out[2]}}, 1'b0}), .out(Sum), .cout(adder_2_cout));  // open: cin
  or or_2 (Final_carry, adder_2_cout, or_1_out[2]);

  // Notes on the sheet:
  //   BCD Adder
  //   Let sum = Cout S3 S2 S1 S0
  //   The sum needs correction when:
  //   Cout = 1 ,i.e., sum > 15
  //   S3 AND S2 ,i.e., 15 >= sum >= 12
  //   S3 AND S1 ,i.e., 11 >= sum >= 10
endmodule
