// Logisim project boolean_func.circ as structural Verilog
module Func (
  input  A,
  input  B,
  input  C,
  input  D,
  output Y
);

  wire and_1_out, and_2_out, not_1_out, not_2_out;

  not not_1 (not_1_out, A);
  not not_2 (not_2_out, C);
  and and_1 (and_1_out, not_1_out, not_2_out);
  and and_2 (and_2_out, A, B, D);
  or or_1 (Y, and_1_out, and_2_out);

  // Notes on the sheet:
  //   Realizing a Boolean Function
  //   F = A'B'C D'+ A'B C D'+ A B C D'+ A B'C D'+ A'B'C' D + A B'C'D + A B'C'D + A B' C D
endmodule
