// Logisim project carry_look_ahead_adder.circ as structural Verilog: 1 circuit, main circuit CLA
module CLA (
  input  [3:0] A,
  input  [3:0] B,
  output S0,
  output S1,
  output S2,
  output S3,
  output Carry,
  output [3:0] Sum
);

  wire and_1_out, and_2_out, and_3_out, and_4_out, G_2_out, G_3_out, G_4_out, G_out, or_2_out, or_3_out,
       or_4_out, P_2_out, P_3_out, P_4_out, P_out, xor_1_out, xor_3_out, xor_5_out, xor_7_out;

  and G (G_out, A[3], B[3]);
  or P (P_out, A[3], B[3]);
  and and_1 (and_1_out, P_out, or_2_out);
  xor xor_1 (xor_1_out, A[3], B[3]);
  or or_1 (Carry, G_out, and_1_out);
  xor xor_2 (S3, xor_1_out, or_2_out);
  or P_2 (P_2_out, A[2], B[2]);
  and G_2 (G_2_out, A[2], B[2]);
  and and_2 (and_2_out, P_2_out, or_3_out);
  xor xor_3 (xor_3_out, A[2], B[2]);
  or or_2 (or_2_out, G_2_out, and_2_out);
  xor xor_4 (S2, xor_3_out, or_3_out);
  or P_3 (P_3_out, A[1], B[1]);
  and G_3 (G_3_out, A[1], B[1]);
  and and_3 (and_3_out, P_3_out, or_4_out);
  xor xor_5 (xor_5_out, A[1], B[1]);
  or or_3 (or_3_out, G_3_out, and_3_out);
  xor xor_6 (S1, xor_5_out, or_4_out);
  or P_4 (P_4_out, A[0], B[0]);
  and G_4 (G_4_out, A[0], B[0]);
  and and_4 (and_4_out, P_4_out, 1'b0);
  xor xor_7 (xor_7_out, A[0], B[0]);
  or or_4 (or_4_out, G_4_out, and_4_out);
  xor xor_8 (S0, xor_7_out, 1'b0);

  assign Sum = {S3, S2, S1, S0};

  // Notes on the sheet:
  //   On the top level, G gates denotes Generator
  //   In the last level, we have half adders
  //   In the middle level, P gates denotes Propagator
  //   Those two are combined according to formula to generate carry
  //   4 BIT CARRY LOOK AHEAD ADDER
  //   Generate: Gi = Ai Bi
  //   Propagate: Pi = Ai + Bi
  //   Carry: Ci = Gii-1 + Pi-1 Ci-1
  //   Sum: Si = Ai ^ Bi ^ Ci
endmodule
