// Logisim project cpu.circ as structural Verilog
module ALU (
  input  [7:0] A,
  input  [7:0] B,
  input  [1:0] Selector,
  output [7:0] Result,
  output Carryout,
  output Borrowout
);

  wire [7:0] adder_1_out, and_1_out, or_1_out, subtractor_1_out;

  Adder adder_1 (.a(B), .b(A), .out(adder_1_out), .cin(1'b0), .cout(Carryout));
  assign or_1_out = A | B;  // OR_Gate or_1, 8 bits wide
  Subtractor subtractor_1 (.a(B), .b(A), .out(subtractor_1_out), .bin(1'b0), .bout(Borrowout));
  assign and_1_out = A & B;  // AND_Gate and_1, 8 bits wide
  Multiplexer #(.select(2), .width(8)) multiplexer_1 (
    .in0(and_1_out), .in1(or_1_out), .in2(adder_1_out), .in3(subtractor_1_out), .out(Result), .sel(Selector));

  // Notes on the sheet:
  //   Subtaction is B - A
  //   00     AND
  //   01     OR
  //   10     ADD
  //   11     SUB
  //   Opcode   Operation
endmodule

module RegisterFile (
  input  WriteData,
  input  ReadData,
  input  Enable,
  input  Clk,
  input  [1:0] WriteSel
);

  Decoder #(.select(2)) decoder_1 (.sel(WriteSel));  // open: out0, out1, out2, out3, en
  Register R0 (.clk(Clk));  // open: D, en, Q, clr
  Register R1 (.clk(Clk));  // open: D, en, Q, clr
  Register R2 (.clk(Clk));  // open: D, en, Q, clr
  Register R3 (.clk(Clk));  // open: D, en, Q, clr
endmodule
