// Logisim project full_adder_demux.circ as structural Verilog: 1 circuit, main circuit main
module main (
  input  A,
  input  B,
  input  Cin,
  output Co,
  output S
);

  wire demultiplexer_1_out1, demultiplexer_1_out2, demultiplexer_1_out3, demultiplexer_1_out4,
       demultiplexer_1_out5, demultiplexer_1_out6, demultiplexer_1_out7;

  or or_1 (Co, demultiplexer_1_out3, demultiplexer_1_out6, demultiplexer_1_out5, demultiplexer_1_out7);
  Demultiplexer #(.select(3)) demultiplexer_1 (
    .out1(demultiplexer_1_out1), .out2(demultiplexer_1_out2), .out3(demultiplexer_1_out3),
    .out4(demultiplexer_1_out4), .out5(demultiplexer_1_out5), .out6(demultiplexer_1_out6),
    .out7(demultiplexer_1_out7), .in(1'b1), .sel({A, B, Cin}));  // open: out0
  or or_2 (S, demultiplexer_1_out1, demultiplexer_1_out2, demultiplexer_1_out4, demultiplexer_1_out7);

  // Notes on the sheet:
  //   Full Adder using 8:1 DEMUX
endmodule
