// Logisim project full_adder_using_mux.circ as structural Verilog: 1 circuit, main circuit main
module main (
  input  Cin,
  input  A,
  input  B
);

  wire multiplexer_1_out, multiplexer_2_out, not_1_out;

  not not_1 (not_1_out, Cin);
  Multiplexer #(.select(2)) multiplexer_1 (
    .in0(Cin), .in1(not_1_out), .in2(not_1_out), .in3(Cin), .out(multiplexer_1_out), .sel({A, B}));
  // RGBLED Sum: pin names not known; wires that end beside it: 1'b0, multiplexer_1_out
  Multiplexer #(.select(2)) multiplexer_2 (
    .in0(1'b0), .in1(Cin), .in2(Cin), .in3(1'b1), .out(multiplexer_2_out), .sel({A, B}));
  // RGBLED Cout: pin names not known; wires that end beside it: {A, B}, multiplexer_2_out

  // Notes on the sheet:
  //   1-bit Full Adder using 4:1 MUX
  //   Cout: I0 = 0, I1 = Cin , I2 = Cin , I3 = 1
  //   Sum: I0 = Cin , I1 = Cin', I2 = Cin' , I3 = Cin
endmodule
