// Logisim project full_subtractor_IC74153.circ as structural Verilog: 1 circuit, main circuit main
module main (
  input  A,
  input  B,
  input  Bin,
  output Diff,
  output Bout
);

  wire n74153_1_pin1, n74153_1_pin4, n74153_1_pin5, n74153_1_pin12;

  _74153 #(.ShowInternalStructure("true")) u_74153_1 (
    .pin1(n74153_1_pin1), .pin2(A), .pin3(Bin), .pin4(n74153_1_pin4), .pin5(n74153_1_pin5), .pin6(Bin),
    .pin7(Bout), .pin15(n74153_1_pin1), .pin14(B), .pin13(Bin), .pin12(n74153_1_pin12),
    .pin11(n74153_1_pin12), .pin10(Bin), .pin9(Diff));
  not not_1 (n74153_1_pin12, Bin);
  not not_2 (n74153_1_pin4, n74153_1_pin5);
  // also tied to GND on the sheet: n74153_1_pin1
  // also tied to VCC on the sheet: n74153_1_pin5

  // Notes on the sheet:
  //   Full Subtractor using 74153 IC
  //   Diff: I0 = Bin, I1 = Bin', I2 = Bin', I3 = Bin
  //   Bout: I0 = Bin, I1 = 1, I2 = 0, I3 = Bin
endmodule
