// Logisim project half_subtractor.circ as structural Verilog: 1 circuit, main circuit HALF SUBTRACTOR
module HALF_SUBTRACTOR (
  input  A,
  input  B,
  output D,
  output Br
);

  wire and_1_out, and_2_out, not_1_out, not_2_out, not_3_out;

  not not_1 (not_1_out, A);
  not not_2 (not_2_out, B);
  not not_3 (not_3_out, A);
  and and_1 (and_1_out, not_1_out, B);
  and and_2 (and_2_out, A, not_2_out);
  and and_3 (Br, not_3_out, B);
  or or_1 (D, and_1_out, and_2_out);

  // Notes on the sheet:
  //   D = A' B + A B'
  //   Br = A' B
  //   HALF SUBTRACTOR
endmodule
