// Logisim project ripple_carry_adder_subtractor.circ as structural Verilog
module _4_BIT_ADDER_SUBTRACTOR (
  input  [3:0] B,
  input  [3:0] A,
  input  ADD_SUB,
  output Overflow,
  output [3:0] SUM_DIFF
);

  wire and_1_out, and_2_out, and_3_out, and_4_out, and_5_out, and_6_out, and_7_out, and_8_out, and_9_out,
       and_10_out, and_11_out, and_12_out, and_13_out, and_14_out, and_15_out, and_16_out, and_17_out,
       and_18_out, and_19_out, and_20_out, and_21_out, and_22_out, and_23_out, and_24_out, and_25_out,
       and_26_out, and_27_out, and_28_out, not_1_out, not_2_out, not_3_out, not_4_out, not_5_out, not_6_out,
       not_7_out, not_8_out, not_9_out, not_10_out, not_11_out, not_12_out, not_13_out, not_14_out,
       not_15_out, not_16_out, not_17_out, not_18_out, not_19_out, not_20_out, not_21_out, not_22_out,
       not_23_out, not_24_out, or_3_out, or_5_out, or_7_out, xor_1_out, xor_2_out, xor_3_out, xor_4_out;

  xor xor_1 (xor_1_out, B[3], ADD_SUB);
  not not_1 (not_1_out, A[3]);
  not not_2 (not_2_out, xor_1_out);
  not not_3 (not_3_out, A[3]);
  not not_4 (not_4_out, or_3_out);
  not not_5 (not_5_out, xor_1_out);
  not not_6 (not_6_out, or_3_out);
  and and_1 (and_1_out, xor_1_out, or_3_out);
  and and_2 (and_2_out, A[3], xor_1_out);
  and and_3 (and_3_out, A[3], or_3_out);
  and and_4 (and_4_out, not_1_out, not_2_out, or_3_out);
  and and_5 (and_5_out, not_3_out, xor_1_out, not_4_out);
  and and_6 (and_6_out, A[3], not_5_out, not_6_out);
  and and_7 (and_7_out, A[3], xor_1_out, or_3_out);
  or or_1 (Overflow, and_1_out, and_2_out, and_3_out);
  xor xor_2 (xor_2_out, B[2], ADD_SUB);
  or or_2 (SUM_DIFF[3], and_4_out, and_5_out, and_6_out, and_7_out);
  not not_7 (not_7_out, A[2]);
  not not_8 (not_8_out, xor_2_out);
  not not_9 (not_9_out, A[2]);
  not not_10 (not_10_out, or_5_out);
  not not_11 (not_11_out, xor_2_out);
  not not_12 (not_12_out, or_5_out);
  and and_8 (and_8_out, xor_2_out, or_5_out);
  and and_9 (and_9_out, A[2], xor_2_out);
  and and_10 (and_10_out, A[2], or_5_out);
  and and_11 (and_11_out, not_7_out, not_8_out, or_5_out);
  and and_12 (and_12_out, not_9_out, xor_2_out, not_10_out);
  and and_13 (and_13_out, A[2], not_11_out, not_12_out);
  and and_14 (and_14_out, A[2], xor_2_out, or_5_out);
  or or_3 (or_3_out, and_8_out, and_9_out, and_10_out);
  or or_4 (SUM_DIFF[2], and_11_out, and_12_out, and_13_out, and_14_out);
  xor xor_3 (xor_3_out, B[1], ADD_SUB);
  not not_13 (not_13_out, A[1]);
  not not_14 (not_14_out, xor_3_out);
  not not_15 (not_15_out, A[1]);
  not not_16 (not_16_out, or_7_out);
  not not_17 (not_17_out, xor_3_out);
  not not_18 (not_18_out, or_7_out);
  and and_15 (and_15_out, xor_3_out, or_7_out);
  and and_16 (and_16_out, A[1], xor_3_out);
  and and_17 (and_17_out, A[1], or_7_out);
  and and_18 (and_18_out, not_13_out, not_14_out, or_7_out);
  and and_19 (and_19_out, not_15_out, xor_3_out, not_16_out);
  and and_20 (and_20_out, A[1], not_17_out, not_18_out);
  and and_21 (and_21_out, A[1], xor_3_out, or_7_out);
  or or_5 (or_5_out, and_15_out, and_16_out, and_17_out);
  xor xor_4 (xor_4_out, B[0], ADD_SUB);
  or or_6 (SUM_DIFF[1], and_18_out, and_19_out, and_20_out, and_21_out);
  not not_19 (not_19_out, A[0]);
  not not_20 (not_20_out, xor_4_out);
  not not_21 (not_21_out, A[0]);
  not not_22 (not_22_out, ADD_SUB);
  not not_23 (not_23_out, xor_4_out);
  not not_24 (not_24_out, ADD_SUB);
  and and_22 (and_22_out, xor_4_out, ADD_SUB);
  and and_23 (and_23_out, A[0], xor_4_out);
  and and_24 (and_24_out, A[0], ADD_SUB);
  and and_25 (and_25_out, not_19_out, not_20_out, ADD_SUB);
  and and_26 (and_26_out, not_21_out, xor_4_out, not_22_out);
  and and_27 (and_27_out, A[0], not_23_out, not_24_out);
  and and_28 (and_28_out, A[0], xor_4_out, ADD_SUB);
  or or_7 (or_7_out, and_22_out, and_23_out, and_24_out);
  or or_8 (SUM_DIFF[0], and_25_out, and_26_out, and_27_out, and_28_out);

  // Notes on the sheet:
  //   First operand A is inputed as it is
  //   4 BIT RIPPLE CARRY ADDER/SUBTRACTOR
  //   This indicates if addition/subtraction is valid or not. 0 means valid else invalid
  //   Second operand B is inputed by doing 2's complement with 'ADD/SUB'  when subtracting 
  //   as a initial carry in
  //   1 : SUBTRACTION
  //   0 : ADDITION
  //   It serves as a switch for addition and subtraction and also act
endmodule
